# Fritzing sketch ATtiny_WS2812_garden_lamp (saved by Fritzing 0.9.3b)
circuit board: 3.33479cm x 3.1168cm

parts:
  ATtiny13 = ATTINY13 [package=dip]
  WS2812B = Neopixel Strip -- Black (30/m)
  R1 = Resistor [tolerance=±5% resistance=220 package=THT]
  Vin = Screw terminal - 2 pins [package=THT]
  7805 = Voltage Regulator [package=to220-igo]
  LDR = Photocell (LDR) [package=THT]
  R3 = Resistor [tolerance=±5% resistance=10k package=THT]
  C1 = Electrolytic Capacitor [capacitance=100µF voltage=16V package="200 mil [THT, electrolytic]"]

nets:
  N1: ATtiny13.PB3(ADC3), LDR.pin_0, R3.Pin_1
  GND: ATtiny13.GND, WS2812B.GND, Vin.pin2, 7805.GND, R3.Pin_0, C1.-
  N2: ATtiny13.PB0(MOSI), R1.Pin_0
  5V: ATtiny13.VCC, WS2812B.+5V, 7805.OUT, LDR.pin_1, C1.+
  N3: WS2812B.Din, R1.Pin_1
  N4: Vin.pin1, 7805.IN

custom parts:
  Neopixel Strip -- Black (30/m): These NeoPixel strips have 30 digitally-addressable pixel LEDs per meter and are very affordable and are only 12.5 mm wide, 10 mm if you remove the strip from the casing.
