# Fritzing sketch Program_ATtiny (saved by Fritzing 0.9.4)
breadboards: 1

parts:
  Bauteil1 = Arduino Nano (Rev3.0)
  ATtiny13_A = ATTINY13 [package=dip]
  C1 = Electrolytic Capacitor [capacitance=10µF package="100 mil [THT, electrolytic]"]

nets:
  N1: Bauteil1.RESET, C1.-
  GND: Bauteil1.GND, ATtiny13_A.GND
  N2: Bauteil1.D9, ATtiny13_A.PB3(ADC3)
  N3: Bauteil1.D10, ATtiny13_A.PB5(NRES)
  N4: Bauteil1.D11/MOSI, ATtiny13_A.PB0(MOSI)
  N5: Bauteil1.D12/MISO, ATtiny13_A.PB1(MISO)
  5V: Bauteil1.5V, ATtiny13_A.VCC, C1.+
  N6: Bauteil1.D13/SCK, ATtiny13_A.PB2(SCK_ADC1)
